// Logisim project 3 input majority.circ as structural Verilog: 1 circuit, main circuit main
module main (
);

  wire and_1_out, and_2_out, and_3_out, or_1_out, undriven, undriven_2, undriven_3;

  and and_1 (and_1_out, undriven, undriven_2);
  and and_2 (and_2_out, undriven_2, undriven_3);
  and and_3 (and_3_out, undriven, undriven_3);
  or or_1 (or_1_out, and_1_out, and_2_out, and_3_out);

  // Notes on the sheet:
  //   B
  //   C
  //   A
endmodule
