// Logisim project 3 to 8 decoder.circ as structural Verilog: 1 circuit, main circuit main
module main (
);

  wire and_1_out, and_2_out, and_3_out, and_4_out, and_5_out, and_6_out, and_7_out, and_8_out, not_1_out,
       not_2_out, not_3_out, undriven, undriven_2, undriven_3, undriven_4;

  not not_1 (not_1_out, undriven);
  not not_2 (not_2_out, undriven_2);
  not not_3 (not_3_out, undriven_3);
  LED led_1 (.in(and_1_out));
  and and_1 (and_1_out, undriven, undriven_2, undriven_3, undriven_4);
  and and_2 (and_2_out, undriven, undriven_2, not_3_out, undriven_4);
  LED led_2 (.in(and_2_out));
  LED led_3 (.in(and_3_out));
  and and_3 (and_3_out, undriven, not_2_out, undriven_3, undriven_4);
  LED led_4 (.in(and_4_out));
  and and_4 (and_4_out, undriven, not_2_out, not_3_out, undriven_4);
  and and_5 (and_5_out, not_1_out, undriven_2, undriven_3, undriven_4);
  LED led_5 (.in(and_5_out));
  LED led_6 (.in(and_6_out));
  and and_6 (and_6_out, not_1_out, undriven_2, not_3_out, undriven_4);
  and and_7 (and_7_out, not_1_out, not_2_out, undriven_3, undriven_4);
  LED led_7 (.in(and_7_out));
  LED led_8 (.in(and_8_out));
  and and_8 (and_8_out, not_1_out, not_2_out, not_3_out, undriven_4);

  // Notes on the sheet:
  //   A
  //   B
  //   C
  //   E
  //   07
  //   06
  //   05
  //   04
  //   03
  //   02
  //   01
  //   00
endmodule
