// Logisim project Clocked SR Latch 2.circ as structural Verilog: 1 circuit, main circuit main
module main (
);

  wire nand_1_out, nand_2_out, nor_1_out, nor_2_out, not_1_out, or_1_out, or_2_out, or_3_out, or_4_out,
       undriven, undriven_2;

  not not_1 (not_1_out, undriven);
  or or_1 (or_1_out, undriven, undriven_2);
  or or_2 (or_2_out, undriven_2, not_1_out);
  nor nor_1 (nor_1_out, or_1_out, nor_2_out);
  nor nor_2 (nor_2_out, nor_1_out, or_2_out);
  or or_3 (or_3_out, undriven_2, nor_1_out);
  or or_4 (or_4_out, nor_2_out, undriven_2);
  nand nand_1 (nand_1_out, or_3_out, nand_2_out);
  nand nand_2 (nand_2_out, nand_1_out, or_4_out);

  // Notes on the sheet:
  //   D
  //   CK
  //   Q
  //   NOT Q
endmodule
