// Logisim project Clocked SR Latch.circ as structural Verilog: 1 circuit, main circuit main
module main (
);

  wire nand_1_out, nand_2_out, not_1_out, not_2_out, not_3_out, not_4_out, or_1_out, or_2_out, undriven,
       undriven_2, xor_1_out;

  not not_1 (not_1_out, undriven);
  not not_2 (not_2_out, not_1_out);
  not not_3 (not_3_out, not_2_out);
  xor xor_1 (xor_1_out, undriven, not_3_out);
  not not_4 (not_4_out, undriven_2);
  or or_1 (or_1_out, undriven_2, xor_1_out);
  or or_2 (or_2_out, xor_1_out, not_4_out);
  nand nand_1 (nand_1_out, or_1_out, nand_2_out);
  nand nand_2 (nand_2_out, nand_1_out, or_2_out);

  // Notes on the sheet:
  //   Input
  //   D
  //   Q
  //   NOT Q
endmodule
