// Logisim project D flip flop w NAND.circ as structural Verilog: 1 circuit, main circuit main
module main (
);

  wire nand_1_out, nand_2_out, nand_3_out, nand_4_out, nand_5_out, undriven, undriven_2;

  nand nand_1 (nand_1_out, undriven, undriven);
  nand nand_2 (nand_2_out, undriven, undriven_2);
  nand nand_3 (nand_3_out, undriven_2, nand_1_out);
  nand nand_4 (nand_4_out, nand_2_out, nand_5_out);
  nand nand_5 (nand_5_out, nand_4_out, nand_3_out);

  // Notes on the sheet:
  //   D
  //   CLOCK
  //   Q
  //   NOT Q
endmodule
